// Logisim project inst logic.circ as structural Verilog
module Parser_de_Inst (
  input  [31:0] in_1
);
endmodule

module Interpreter_OPCOde (
  input  [5:0] Opcode
);
endmodule
